// Logisim project Alarm_and_Fan-Replace.circ as structural Verilog: 1 circuit, main circuit main
module main (
  input  Cord,
  input  Low_Voltage,
  input  Temp,
  output Alarm,
  output Fan
);


  assign Alarm = Cord;
  assign Fan = Low_Voltage;
endmodule
