// Logisim project SSI-7400-NAND-replace.circ as structural Verilog: 1 circuit, main circuit main
module main (
  input  A,
  input  B,
  input  C,
  input  D,
  output out_5
);

  // _7400 7400_1: pin names not known; wires that end beside it: A, B, C, D, out_5
endmodule
