// Logisim project SSI-7400-NAND-replaceEW.circ as structural Verilog: 1 circuit, main circuit main
module main (
  input  A,
  input  B,
  input  C,
  input  D,
  output out_5
);

  wire n7400_1_p4, n7400_1_p7, n7400_1_p12;

  // _7400 7400_1: pin names not known; wires that end beside it: A, B, B, n7400_1_p4, D, D, n7400_1_p7, 1'b0, 1'b1, n7400_1_p4, n7400_1_p7, n7400_1_p12, n7400_1_p12, C, out_5
endmodule
