// Logisim project SSI-7400-replace.circ as structural Verilog: 1 circuit, main circuit main
module main (
  input  A,
  input  B,
  input  C,
  input  D,
  output out_5
);

  // _7408 7408_1: pin names not known; wires that end beside it: A
  // _7404 7404_1: pin names not known; wires that end beside it: B, C, D
  // _7432 7432_1: pin names not known; wires that end beside it: out_5
endmodule
