// Logisim project SSI-7400-replaceEW.circ as structural Verilog: 1 circuit, main circuit main
module main (
  input  A,
  input  B,
  input  C,
  input  D,
  output out_5
);

  wire n7404_1_p2, n7408_1_p3;

  // _7408 7408_1: pin names not known; wires that end beside it: A, C, n7408_1_p3, 1'b1
  // _7404 7404_1: pin names not known; wires that end beside it: 1'b0, n7404_1_p2, 1'b0, 1'b1, n7404_1_p2, out_5
  // _7432 7432_1: pin names not known; wires that end beside it: B, D, n7408_1_p3, 1'b0, 1'b1
endmodule
