// Logisim project SSI-replaceEw.circ as structural Verilog: 1 circuit, main circuit SSI
module SSI (
  input  A,
  input  B,
  input  C,
  input  D,
  output X
);

  wire and_1_out, not_1_out, not_2_out, or_1_out;

  or or_1 (or_1_out, B, D);
  not not_1 (not_1_out, or_1_out);
  not not_2 (not_2_out, not_1_out);
  and and_1 (and_1_out, C, not_2_out);
  not not_3 (X, and_1_out);
endmodule
