// Logisim project SSI-replaceNandEW.circ as structural Verilog: 1 circuit, main circuit SSI
module SSI (
  input  A,
  input  B,
  input  C,
  input  D,
  output X
);

  wire nand_1_out, nand_2_out, nand_3_out;

  nand nand_1 (nand_1_out, B, B);
  nand nand_2 (nand_2_out, nand_1_out, nand_3_out);
  nand nand_3 (nand_3_out, D, D);
  nand nand_4 (X, C, nand_2_out);
endmodule
