// Logisim project ewAlarm_and_Fan-Replace.circ as structural Verilog: 1 circuit, main circuit main
module main (
  input  Cord,
  input  Low_Voltage,
  input  Temp,
  output Alarm,
  output Fan
);

  wire and_2_out, and_3_out, not_1_out, not_2_out;

  not not_1 (not_1_out, Cord);
  and and_1 (Alarm, not_1_out, Low_Voltage);
  not not_2 (not_2_out, Low_Voltage);
  and and_2 (and_2_out, not_2_out, Temp);
  and and_3 (and_3_out, Low_Voltage, Cord, Temp);
  or or_1 (Fan, and_2_out, and_3_out);
endmodule
